// Logisim project ALU COMP2.circ as structural Verilog: 1 circuit, main circuit main
module main (
  input  ADD,
  input  [15:0] in_2,
  input  [15:0] in_3,
  input  SUB,
  input  OR,
  input  AND,
  input  XOR,
  input  COMP,
  input  SHL,
  input  SHR,
  input  DRTAC,
  output [15:0] out_12
);

  wire [3:0] bit_extender_1_out, bit_extender_2_out;
  wire [15:0] adder_1_out, and_1_out, and_2_out, and_3_out, and_4_out, and_5_out, and_6_out, and_7_out,
       and_8_out, and_9_out, and_10_out, not_1_out, or_1_out, or_2_out, or_3_out, shifter_1_out,
       shifter_2_out, subtractor_1_out, xor_1_out;

  Adder #(.width(16)) adder_1 (.a(in_3), .b(in_2), .out(adder_1_out));  // open: cin, cout
  Subtractor #(.width(16)) subtractor_1 (.a(in_2), .b(in_3), .out(subtractor_1_out));  // open: bin, bout
  assign or_1_out = in_3 | in_2;  // OR_Gate or_1, 16 bits wide
  assign not_1_out = ~in_2;  // NOT_Gate not_1, 16 bits wide
  assign bit_extender_1_out = {{3{1'b0}}, 1'b1};  // Bit_Extender bit_extender_1
  assign bit_extender_2_out = {{3{1'b0}}, 1'b1};  // Bit_Extender bit_extender_2
  assign and_1_out = in_3 & in_2;  // AND_Gate and_1, 16 bits wide
  assign xor_1_out = in_3 ^ in_2;  // XOR_Gate xor_1, 16 bits wide
  Shifter #(.width(16)) shifter_1 (.in(in_2), .\dist (bit_extender_1_out), .out(shifter_1_out));
  Shifter #(.width(16), .shift("lr")) shifter_2 (.in(in_2), .\dist (bit_extender_2_out), .out(shifter_2_out));
  assign and_2_out = {16{ADD}} & adder_1_out;  // AND_Gate and_2, 16 bits wide
  assign and_3_out = {16{SUB}} & subtractor_1_out;  // AND_Gate and_3, 16 bits wide
  assign and_4_out = {16{OR}} & or_1_out;  // AND_Gate and_4, 16 bits wide
  assign and_5_out = {16{AND}} & and_1_out;  // AND_Gate and_5, 16 bits wide
  assign and_6_out = {16{XOR}} & xor_1_out;  // AND_Gate and_6, 16 bits wide
  assign and_7_out = {16{COMP}} & not_1_out;  // AND_Gate and_7, 16 bits wide
  assign and_8_out = {16{SHL}} & shifter_1_out;  // AND_Gate and_8, 16 bits wide
  assign and_9_out = {16{DRTAC}} & in_3;  // AND_Gate and_9, 16 bits wide
  assign and_10_out = {16{SHR}} & shifter_2_out;  // AND_Gate and_10, 16 bits wide
  assign or_2_out = and_2_out | and_3_out | and_4_out | and_5_out;  // OR_Gate or_2, 16 bits wide
  assign or_3_out = and_6_out | and_7_out | and_8_out | and_10_out;  // OR_Gate or_3, 16 bits wide
  assign out_12 = or_2_out | or_3_out | and_9_out;  // OR_Gate or_4, 16 bits wide

  // Notes on the sheet:
  //   AC
  //   DR
endmodule
