// Logisim project Computer 2.circ as structural Verilog: 1 circuit, main circuit main
module main (
  output [6:0] out_1,
  output [15:0] out_2
);

  wire and_3_out, and_4_out, AR_p2, AR_p4, counter_1_q, main_1_p4, main_1_p8, main_1_p9, main_1_p10,
       main_1_p11, main_1_p12, main_1_p13, main_1_p14, main_1_p15, main_1_p16, main_1_p17, main_1_p18,
       main_1_p19, main_1_p21, main_1_p23, main_1_p24, main_1_p25, main_1_p26, not_1_out, not_2_out,
       or_2_out, PC_p2, PC_p3, SBR_p2;
  wire [1:0] main_1_p20;
  wire [2:0] main_1_p5, main_1_p6;
  wire [3:0] DR_p5_2;
  wire [6:0] and_1_out, and_2_out, CAR_p4, CAR_p9, main_2_car_input, SBR_p1;
  wire [6:6] decoder_1_out0, decoder_1_out1;
  wire [10:0] AR_p1, AR_p5, bit_extender_1_out, CAR_p5;
  wire [13:0] rom_1_data;
  wire [15:0] bit_extender_2_out, DR_p1, DR_p5, main_3_out_12, ram_1_data;

  // _7_bit_Register_main SBR: pin names not known; wires that end beside it: SBR_p1, SBR_p2, 1'b0
  Counter #(.width(1), .max('h1), .ongoal("stay")) counter_1 (
    .Q(counter_1_q), .clk(AR_p4));  // open: load, D, count, carry, clr
  Decoder #(.enable("false")) decoder_1 (.out0(decoder_1_out0[6]), .out1(decoder_1_out1[6]), .sel(counter_1_q));
  // _11_bit_Register_main AR: pin names not known; wires that end beside it: AR_p1, AR_p2, 1'b0, AR_p4, AR_p5
  // _11_bit_Register_main PC: pin names not known; wires that end beside it: AR_p5, PC_p2, PC_p3
  assign and_1_out = {7{decoder_1_out0[6]}} & 7'b1000000;  // AND_Gate and_1, 7 bits wide
  assign and_2_out = {7{decoder_1_out1[6]}} & main_2_car_input;  // AND_Gate and_2, 7 bits wide
  Multiplexer #(.width(11), .enable("false")) multiplexer_1 (
    .in0(CAR_p5), .in1(bit_extender_1_out), .out(AR_p1), .sel(main_1_p4));
  not not_1 (not_1_out, and_4_out);
  and and_3 (and_3_out, not_1_out, not_2_out);
  not not_2 (not_2_out, main_1_p26);
  // Control_Unit_COMP2_main main_1: pin names not known; wires that end beside it: PC_p3, PC_p2, AR_p2, main_1_p4, main_1_p5, main_1_p6, rom_1_data[13:11], main_1_p8, main_1_p9, main_1_p10, main_1_p11, main_1_p12, main_1_p13, main_1_p14, main_1_p15, main_1_p16, main_1_p17, main_1_p18, main_1_p19, main_1_p20[0], main_1_p21, main_1_p20[1], main_1_p23, main_1_p24, main_1_p25, main_1_p26
  Bit_Extender #(.in_width(16), .out_width(11)) bit_extender_1 (
    .in({DR_p5[15], DR_p5_2, DR_p5[10:0]}), .out(bit_extender_1_out));
  // _7_bit_Register_main CAR: pin names not known; wires that end beside it: AR_p4, out_1, AR_p4, CAR_p4, CAR_p5, 1'b1, 1'b0, AR_p4, CAR_p9
  assign CAR_p4 = and_1_out | and_2_out;  // OR_Gate or_1, 7 bits wide
  ROM #(.addrWidth(7), .dataWidth(20)) rom_1 (
    .addr(CAR_p9), .data({main_1_p5, main_1_p6, rom_1_data}), .sel(and_3_out));
  and and_4 (and_4_out, rom_1_data[11], rom_1_data[12], rom_1_data[13]);
  MicroProgram_Sequencer_COMP2_main main_2 (
    .DR_11_14(DR_p5_2), .SBR_OUTPUT(out_1), .in_15(DR_p5[15]), .AC(out_2), .CAR_OUTPUT(CAR_p9),
    .SBR_INPUT(SBR_p1), .LD_SBR(SBR_p2), .CD_10(rom_1_data[10]), .BR_8(rom_1_data[9]), .AD_6(rom_1_data[8]),
    .in_7(rom_1_data[7]), .AD_4(rom_1_data[6]), .AD_5(rom_1_data[5]), .AD_2(rom_1_data[4]),
    .AD_3(rom_1_data[3]), .AD_0(rom_1_data[2]), .AD_1(rom_1_data[1]), .in_14(rom_1_data[0]),
    .CAR_INPUT(main_2_car_input));
  or or_2 (or_2_out, main_1_p25, main_1_p24);
  assign bit_extender_2_out = {{5{1'b0}}, CAR_p5};  // Bit_Extender bit_extender_2
  // _16_bit_Register_main DR: pin names not known; wires that end beside it: DR_p1, main_1_p21, main_1_p23, AR_p4, {DR_p5[15], DR_p5_2, DR_p5[10:0]}
  ALU_COMP2_main main_3 (
    .out_12(main_3_out_12), .in_2(out_2), .in_3({DR_p5[15], DR_p5_2, DR_p5[10:0]}), .ADD(main_1_p8),
    .SUB(main_1_p9), .OR(main_1_p10), .AND(main_1_p11), .XOR(main_1_p12), .COMP(main_1_p13),
    .SHL(main_1_p15), .SHR(main_1_p16), .DRTAC(main_1_p17));
  // _16_bit_Register_main AC: pin names not known; wires that end beside it: main_3_out_12, main_1_p14, main_1_p18, main_1_p19, AR_p4, out_2
  Multiplexer #(.select(2), .width(16), .enable("false")) multiplexer_2 (
    .in0(ram_1_data), .in1(out_2), .in2(bit_extender_2_out), .out(DR_p1), .sel(main_1_p20));  // open: in3
  RAM #(.addrWidth(11), .dataWidth(16), .bus("separate")) ram_1 (
    .addr(AR_p5), .din({DR_p5[15], DR_p5_2, DR_p5[10:0]}), .data(ram_1_data), .str(main_1_p24),
    .sel(or_2_out), .clk(AR_p4), .ld(main_1_p25));  // open: clr
  Clock clock_1 (.out(AR_p4));

  // Notes on the sheet:
  //   contents of rom_1 (hex, n*v repeats v):
  //   2c3 10002 20040 40 406 40 2c3 3040 2c3 1400a e0040 40 2c3 1000e 9400f e0040 16*0 3800 31*0 c0041
  //   12842 a01a0 a0130 a0120
endmodule
