// Logisim project MicroProgram Sequencer COMP2.circ as structural Verilog: 1 circuit, main circuit main
module main (
  input  [3:0] DR_11_14,
  input  [15:0] AC,
  input  [6:0] SBR_OUTPUT,
  input  CD_10,
  input  BR_8,
  input  AD_6,
  input  in_7,
  input  AD_4,
  input  AD_5,
  input  AD_2,
  input  AD_3,
  input  AD_0,
  input  AD_1,
  input  in_14,
  input  in_15,
  input  [6:0] CAR_OUTPUT,
  output [6:0] SBR_INPUT,
  output [6:0] CAR_INPUT,
  output LD_SBR
);

  wire multiplexer_1_out, or_1_out, or_2_out, or_3_out, or_4_out;
  wire [1:0] main_1_p5;

  or or_1 (or_1_out, AC[14], AC[13], AC[12], AC[11], AC[10]);
  or or_2 (or_2_out, AC[9], AC[8], AC[7], AC[6], AC[5]);
  or or_3 (or_3_out, AC[15], or_1_out, or_2_out, or_4_out);
  or or_4 (or_4_out, AC[4], AC[3], AC[2], AC[1], AC[0]);
  Multiplexer #(.select(2), .enable("false")) multiplexer_1 (
    .in0(1'b1), .in1(in_15), .in2(AC[15]), .in3(or_3_out), .out(multiplexer_1_out), .sel({CD_10, BR_8}));
  // Input_Logic_COMP2_main main_1: pin names not known; wires that end beside it: AD_6, in_7, multiplexer_1_out, main_1_p5[1], main_1_p5[0], LD_SBR
  Multiplexer #(.select(2), .width(7), .enable("false")) multiplexer_2 (
    .in0(SBR_INPUT), .in1({AD_4, AD_5, AD_2, AD_3, AD_0, AD_1, in_14}), .in2(SBR_OUTPUT),
    .in3({1'b0, DR_11_14, 2'b00}), .out(CAR_INPUT), .sel(main_1_p5));
  Adder #(.width(7)) adder_1 (.a(CAR_OUTPUT), .b(7'b0000001), .out(SBR_INPUT));  // open: cin, cout

  // Notes on the sheet:
  //   CD[9]
  //   BR[7]
endmodule
